// Logisim project part1.circ as structural Verilog: 6 circuits, main circuit main
module main (
  input  in_1,
  input  in_2,
  input  in_3,
  input  in_4,
  input  in_5,
  input  in_6,
  input  in_7,
  input  in_8,
  input  in_9,
  input  in_10,
  input  in_11,
  input  in_12,
  input  in_13,
  input  in_14,
  input  in_15,
  output out_16,
  output out_17,
  output out_18,
  output out_19,
  output out_20
);

  NOR1 NOR_Gate (.In1(in_1), .In2(in_2), .Out1(out_16));
  NAND1 NAND_Gate (.In1(in_3), .In2(in_4), .Out1(out_17));
  XOR1 XOR_Gate (.In1(in_5), .In2(in_6), .Out1(out_18));
  Two2OneMUX Two2OneMUXGate (.InA(in_7), .InX(in_8), .InB(in_9), .out_4(out_19));
  Four2OneMUX Four2OneMUXGate (
    .In0(in_10), .In1(in_11), .X0(in_12), .X1(in_13), .In2(in_14), .In3(in_15), .out_7(out_20));
endmodule

module NAND1 (
  input  In1,
  input  In2,
  output Out1
);

  wire and_1_out;

  and and_1 (and_1_out, In1, In2);
  not not_1 (Out1, and_1_out);
endmodule

module NOR1 (
  input  In1,
  input  In2,
  output Out1
);

  wire or_1_out;

  or or_1 (or_1_out, In1, In2);
  not not_1 (Out1, or_1_out);
endmodule

module XOR1 (
  input  In1,
  input  In2,
  output Out1
);

  wire nand1_1_out1, or_1_out;

  or or_1 (or_1_out, In1, In2);
  NAND1 nand1_1 (.In1(In1), .In2(In2), .Out1(nand1_1_out1));
  and and_1 (Out1, or_1_out, nand1_1_out1);

  // Notes on the sheet:
  //   A+B
  //   NOT (A AND B)
endmodule

module Two2OneMUX (
  input  InA,
  input  InX,
  input  InB,
  output out_4
);

  wire and_1_out, and_2_out, not_1_out;

  not not_1 (not_1_out, InX);
  and and_1 (and_1_out, not_1_out, InA);
  and and_2 (and_2_out, InB, InX);
  or or_1 (out_4, and_1_out, and_2_out);

  // Notes on the sheet:
  //   Output = (A AND ~X) OR (B AND X)
endmodule

module Four2OneMUX (
  input  In0,
  input  In1,
  input  X0,
  input  X1,
  input  In2,
  input  In3,
  output out_7
);

  wire two2onemux_1_out_4, two2onemux_2_out_4;

  Two2OneMUX two2onemux_1 (.InA(In0), .InX(X0), .InB(In1), .out_4(two2onemux_1_out_4));
  Two2OneMUX two2onemux_2 (.InA(In2), .InX(X0), .InB(In3), .out_4(two2onemux_2_out_4));
  Two2OneMUX two2onemux_3 (.InA(two2onemux_1_out_4), .InX(X1), .InB(two2onemux_2_out_4), .out_4(out_7));
endmodule
