// Logisim project part2.circ as structural Verilog: 2 circuits, main circuit main
module main (
  output [7:0] AdderOut,
  output [7:0] RegisterOut
);

  AddMachine addmachine_1 (.out_1(AdderOut), .out_2(RegisterOut));
endmodule

module AddMachine (
  output [7:0] out_1,
  output [7:0] out_2
);

  wire clock1_out;

  Adder adder_1 (.a(8'h1), .b(out_2), .out(out_1));  // open: cin, cout
  Clock clock1 (.out(clock1_out));
  Register register_1 (.D(out_1), .clk(clock1_out), .Q(out_2));  // open: en, clr
endmodule
