// Logisim project part4_5.circ as structural Verilog
module Ex4 (
  input  [7:0] In1,
  output Out1,
  output [7:0] Out2
);

  and and_1 (Out1, In1[0], In1[7]);
  not not_1 (Out2[7], In1[7]);

  assign Out2[6:0] = In1[6:0];

  // Notes on the sheet:
  //   If Out1 = 1, the input # is negative and odd
endmodule

module rotr (
  input  [3:0] InputB,
  input  [15:0] InputA,
  output [15:0] Output1
);

  wire [15:0] multiplexer_1_out, multiplexer_2_out, multiplexer_3_out;

  Multiplexer #(.width(16), .enable("false")) multiplexer_1 (
    .in0(InputA), .in1({InputA[7:0], InputA[15:8]}), .out(multiplexer_1_out), .sel(InputB[3]));
  Multiplexer #(.width(16), .enable("false")) multiplexer_2 (
    .in0(multiplexer_1_out), .in1({multiplexer_1_out[3:0], multiplexer_1_out[15:4]}),
    .out(multiplexer_2_out), .sel(InputB[2]));
  Multiplexer #(.width(16), .enable("false")) multiplexer_3 (
    .in0(multiplexer_2_out), .in1({multiplexer_2_out[1:0], multiplexer_2_out[15:2]}),
    .out(multiplexer_3_out), .sel(InputB[1]));
  Multiplexer #(.width(16), .enable("false")) multiplexer_4 (
    .in0(multiplexer_3_out), .in1({multiplexer_3_out[0], multiplexer_3_out[15:1]}), .out(Output1),
    .sel(InputB[0]));

  // Notes on the sheet:
  //   NOT shifting by 8
  //   NOT shifting by 4
  //   shifting by 8
  //   NOT shifting by 2
  //   NOT shifting by 1
  //   shifting by 4
  //   shifting by 2
  //   shifting by 1
  //   shifting by 5 = shifting by 4 + shifting by 1
endmodule
