// Logisim project alu.circ as structural Verilog: 1 circuit, main circuit alu
module alu (
  input  [31:0] A,
  input  [31:0] B,
  input  [3:0] ALUSel,
  output [31:0] Result
);

  wire comparator_1_lt;
  wire [31:0] add, and1, divu1, mul1, mulh1, mulhu1, or1, remu1, sll1, slt1, sra1, srl1, sub1, vaddh1, xor1;

  Multiplexer #(.select(4), .width(32), .enable("false")) multiplexer_1 (
    .in0(add), .in1(and1), .in2(or1), .in3(xor1), .in4(srl1), .in5(sra1), .in6(sll1), .in7(slt1),
    .in8(divu1), .in9(remu1), .in10(mul1), .in11(mulhu1), .in12(sub1), .in13(B), .in14(mulh1), .in15(vaddh1),
    .out(Result), .sel(ALUSel));
  Adder #(.width(32)) adder_1 (.a(A), .b(B), .out(add));  // open: cin, cout
  assign and1 = A & B;  // AND_Gate and_1, 32 bits wide
  assign or1 = A | B;  // OR_Gate or_1, 32 bits wide
  assign xor1 = A ^ B;  // XOR_Gate xor_1, 32 bits wide
  Shifter #(.width(32), .shift("lr")) shifter_1 (.in(A), .\dist (B[4:0]), .out(srl1));
  Shifter #(.width(32), .shift("ar")) shifter_2 (.in(A), .\dist (B[4:0]), .out(sra1));
  Shifter #(.width(32)) shifter_3 (.in(A), .\dist (B[4:0]), .out(sll1));
  Comparator #(.width(32)) comparator_1 (.a(A), .b(B), .lt(comparator_1_lt));  // open: gt, eq
  assign slt1 = {{31{1'b0}}, comparator_1_lt};  // Bit_Extender bit_extender_1
  Multiplier #(.width(32)) multiplier_1 (.a(A), .b(B), .cout(mulh1));  // open: out, cin
  Adder #(.width(16)) adder_2 (.a(A[15:0]), .b(B[15:0]), .out(vaddh1[15:0]));  // open: cin, cout
  Adder #(.width(16)) adder_3 (.a(A[31:16]), .b(B[31:16]), .out(vaddh1[31:16]));  // open: cin, cout
  Divider #(.width(32)) divider_1 (.a(A), .b(B), .out(divu1));  // open: upper, rem
  Divider #(.width(32)) divider_2 (.a(A), .b(B), .rem(remu1));  // open: out, upper
  Multiplier #(.width(32)) multiplier_2 (.a(A), .b(B), .out(mul1));  // open: cin, cout
  Multiplier #(.width(32)) multiplier_3 (.a(A), .b(B), .cout(mulhu1));  // open: out, cin
  Subtractor #(.width(32)) subtractor_1 (.a(A), .b(B), .out(sub1));  // open: bin, bout

  // Other names for the same wires on the sheet: bsel1[31:0] = B

  // Notes on the sheet:
  //   INPUTS to your circuit
  //   DON'T CHANGE THE LOCATIONS OF THE INPUTS AND OUTPUTS!
  //   OUTPUT from your circuit
endmodule
