// Logisim project regfile.circ as structural Verilog: 2 circuits, main circuit main
module main (
  input  [4:0] rs1,
  input  [4:0] rs2,
  input  [4:0] rd,
  input  [31:0] Write_Data,
  input  RegWEn,
  input  clk,
  output [31:0] Read_Data_1,
  output [31:0] ra,
  output [31:0] sp,
  output [31:0] t0,
  output [31:0] t1,
  output [31:0] t2,
  output [31:0] s0,
  output [31:0] s1,
  output [31:0] a0,
  output [31:0] Read_Data_2
);

  wire a0_w_enable, ra_w_enable, s0_w_enable, s1_w_enable, sp_w_enable, t0_w_enable, t1_w_enable, t2_w_enable;

  Demultiplexer #(.select(5), .enable("false")) demultiplexer_1 (
    .out1(ra_w_enable), .out2(sp_w_enable), .out5(t0_w_enable), .out6(t1_w_enable), .out7(t2_w_enable),
    .out8(s0_w_enable), .out9(s1_w_enable), .out10(a0_w_enable), .in(RegWEn), .sel(rd));  // open: out0, out3, out4, out11, out12, out13, out14, out15, out16, out17, out18, out19, out20, out21, out22, out23, out24, out25, out26, out27, out28, out29, out30, out31
  Register #(.width(32)) register_1 (.D(Write_Data), .en(ra_w_enable), .clk(clk), .Q(ra));  // open: clr
  Register #(.width(32)) register_2 (.D(Write_Data), .en(sp_w_enable), .clk(clk), .Q(sp));  // open: clr
  Register #(.width(32)) register_3 (.D(Write_Data), .en(t0_w_enable), .clk(clk), .Q(t0));  // open: clr
  Register #(.width(32)) register_4 (.D(Write_Data), .en(t1_w_enable), .clk(clk), .Q(t1));  // open: clr
  Register #(.width(32)) register_5 (.D(Write_Data), .en(t2_w_enable), .clk(clk), .Q(t2));  // open: clr
  Register #(.width(32)) register_6 (.D(Write_Data), .en(s0_w_enable), .clk(clk), .Q(s0));  // open: clr
  Register #(.width(32)) register_7 (.D(Write_Data), .en(s1_w_enable), .clk(clk), .Q(s1));  // open: clr
  Register #(.width(32)) register_8 (.D(Write_Data), .en(a0_w_enable), .clk(clk), .Q(a0));  // open: clr
  Multiplexer #(.select(5), .width(32), .enable("false")) multiplexer_1 (
    .in0({32{1'b0}}), .in1(ra), .in2(sp), .in5(t0), .in6(t1), .in7(t2), .in8(s0), .in9(s1), .in10(a0),
    .out(Read_Data_1), .sel(rs1));  // open: in3, in4, in11, in12, in13, in14, in15, in16, in17, in18, in19, in20, in21, in22, in23, in24, in25, in26, in27, in28, in29, in30, in31
  Multiplexer #(.select(5), .width(32), .enable("false")) multiplexer_2 (
    .in0({32{1'b0}}), .in1(ra), .in2(sp), .in5(t0), .in6(t1), .in7(t2), .in8(s0), .in9(s1), .in10(a0),
    .out(Read_Data_2), .sel(rs2));  // open: in3, in4, in11, in12, in13, in14, in15, in16, in17, in18, in19, in20, in21, in22, in23, in24, in25, in26, in27, in28, in29, in30, in31

  // Other names for the same wires on the sheet: read_data1[31:0] = Read_Data_1; read_data2[31:0] = Read_Data_2;
  //   read_reg1[4:0] = rs1; read_reg2[4:0] = rs2; write_en = RegWEn; write_reg[4:0] = rd

  // Notes on the sheet:
  //   INPUTS to your circuit
  //   DON'T CHANGE THE LOCATIONS OF THE INPUTS AND OUTPUTS!
  //   These are DEBUG/TEST outputs from your circuit.
  //   OUTPUTS from your circuit
endmodule

module temp (
);

  wire clk, write_en;
  wire [4:0] write_reg;
  wire [31:0] a0, ra, register_1_q, register_2_q, s0, s1, sp, t0, t1, t2, write_data;

  Register #(.width(32)) register_1 (.D(write_data), .en(write_en), .clk(clk), .Q(register_1_q));  // open: clr
  Register #(.width(32)) register_2 (.D(write_data), .en(write_en), .clk(clk), .Q(register_2_q));  // open: clr
  Demultiplexer #(.select(5), .width(32), .enable("false")) demultiplexer_1 (
    .out1(ra), .out2(sp), .out5(t0), .out6(t1), .out7(t2), .out8(s0), .out9(s1), .out10(a0),
    .in(register_1_q), .sel(write_reg));  // open: out0, out3, out4, out11, out12, out13, out14, out15, out16, out17, out18, out19, out20, out21, out22, out23, out24, out25, out26, out27, out28, out29, out30, out31
  Register #(.width(32)) register_3 (.D(write_data), .en(write_en), .clk(clk), .Q(ra));  // open: clr
  Register #(.width(32)) register_4 (.D(write_data), .en(write_en), .clk(clk), .Q(sp));  // open: clr
  Register #(.width(32)) register_5 (.D(write_data), .en(write_en), .clk(clk), .Q(t0));  // open: clr
  Register #(.width(32)) register_6 (.D(write_data), .en(write_en), .clk(clk), .Q(t1));  // open: clr
  Demultiplexer #(.select(5), .width(32), .enable("false")) demultiplexer_2 (
    .out1(ra), .out2(sp), .out5(t0), .out6(t1), .out7(t2), .out8(s0), .out9(s1), .out10(a0),
    .in(register_2_q), .sel(write_reg));  // open: out0, out3, out4, out11, out12, out13, out14, out15, out16, out17, out18, out19, out20, out21, out22, out23, out24, out25, out26, out27, out28, out29, out30, out31
  Register #(.width(32)) register_7 (.D(write_data), .en(write_en), .clk(clk), .Q(t2));  // open: clr
  Register #(.width(32)) register_8 (.D(write_data), .en(write_en), .clk(clk), .Q(s0));  // open: clr
  Register #(.width(32)) register_9 (.D(write_data), .en(write_en), .clk(clk), .Q(s1));  // open: clr
  Register #(.width(32)) register_10 (.D(write_data), .en(write_en), .clk(clk), .Q(a0));  // open: clr
endmodule
