// Logisim project cpu.circ as structural Verilog: 4 circuits, main circuit main
module main (
  input  [31:0] INSTRUCTION,
  input  CLOCK,
  output [31:0] FETCH_ADDRESS,
  output [31:0] ra,
  output [31:0] sp,
  output [31:0] t0,
  output [31:0] t1,
  output [31:0] t2,
  output [31:0] s0,
  output [31:0] s1,
  output [31:0] a0
);

  wire and_1_out, and_2_out, and_3_out, and_4_out, and_5_out, and_6_out, ASel, BrEq, BrLt, BSel, lb, lh, lw,
       MemRW, PCSel, RegWEn, rem0, rem1, rem2, rem3;
  wire [1:0] WBSel;
  wire [3:0] ALUSel;
  wire [31:0] adder_2_out, ALUOut, bit_extender_1_out, bit_extender_2_out, bit_extender_3_out,
       bit_extender_4_out, bit_extender_5_out, bit_extender_6_out, divider_1_rem, DMEMOut, DMEMOutNew, imm,
       InstrWithPipeline, multiplexer_1_out, multiplexer_2_out, multiplexer_3_out, multiplexer_4_out,
       PC_add_4, PCWithPipeline, ReadData1, ReadData2, wb;

  Adder #(.width(32)) adder_1 (.a(FETCH_ADDRESS), .b(32'h4), .out(PC_add_4));  // open: cin, cout
  Multiplexer #(.width(32), .enable("false")) multiplexer_1 (
    .in0(PC_add_4), .in1(ALUOut), .out(multiplexer_1_out), .sel(PCSel));
  Register #(.width(32)) PC (.D(multiplexer_1_out), .clk(CLOCK), .Q(FETCH_ADDRESS));  // open: en, clr
  Register #(.width(32)) register_1 (.D(FETCH_ADDRESS), .clk(CLOCK), .Q(PCWithPipeline));  // open: en, clr
  Control control_1 (
    .Instruction(InstrWithPipeline), .ReadData1(ReadData1), .ReadData2(ReadData2), .PCSel(PCSel),
    .RegWEn(RegWEn), .BrEq(BrEq), .BrLt(BrLt), .ASel(ASel), .BSel(BSel), .ALUSel(ALUSel), .MemRW(MemRW),
    .WBSel(WBSel));
  Register #(.width(32)) register_2 (.D(multiplexer_2_out), .clk(CLOCK), .Q(InstrWithPipeline));  // open: en, clr
  Multiplexer #(.width(32), .enable("false")) multiplexer_2 (
    .in0(INSTRUCTION), .in1(32'h13), .out(multiplexer_2_out), .sel(PCSel));
  regfile_main RegFile (
    .rs2(InstrWithPipeline[24:20]), .rd(InstrWithPipeline[11:7]), .Read_Data_1(ReadData1),
    .Read_Data_2(ReadData2), .ra(ra), .sp(sp), .t0(t0), .t1(t1), .t2(t2), .s0(s0), .s1(s1), .a0(a0),
    .rs1(InstrWithPipeline[19:15]), .Write_Data(wb), .RegWEn(RegWEn), .clk(CLOCK));
  ImmGenerator immgenerator_1 (.Instruction(InstrWithPipeline), .ImmSel(InstrWithPipeline[6:2]), .out_3(imm));
  Multiplexer #(.width(32), .enable("false")) multiplexer_3 (
    .in0(ReadData1), .in1(PCWithPipeline), .out(multiplexer_3_out), .sel(ASel));
  Multiplexer #(.width(32), .enable("false")) multiplexer_4 (
    .in0(ReadData2), .in1(imm), .out(multiplexer_4_out), .sel(BSel));
  Divider #(.width(32)) divider_1 (.a(imm), .b(32'h4), .rem(divider_1_rem));  // open: out, upper
  Comparator #(.width(2)) comparator_1 (.a(divider_1_rem[1:0]), .b(2'b00), .eq(rem0));  // open: gt, lt
  Comparator #(.width(2)) comparator_2 (.a(divider_1_rem[1:0]), .b(2'b01), .eq(rem1));  // open: gt, lt
  Comparator #(.width(2)) comparator_3 (.a(divider_1_rem[1:0]), .b(2'b10), .eq(rem2));  // open: gt, lt
  Comparator #(.width(2)) comparator_4 (.a(divider_1_rem[1:0]), .b(2'b11), .eq(rem3));  // open: gt, lt
  alu Arithmetic_Logic_Unit (.A(multiplexer_3_out), .B(multiplexer_4_out), .ALUSel(ALUSel), .Result(ALUOut));
  Comparator #(.width(3)) comparator_5 (.a(InstrWithPipeline[14:12]), .b(3'b000), .eq(lb));  // open: gt, lt
  Comparator #(.width(3)) comparator_6 (.a(InstrWithPipeline[14:12]), .b(3'b001), .eq(lh));  // open: gt, lt
  Comparator #(.width(3)) comparator_7 (.a(InstrWithPipeline[14:12]), .b(3'b010), .eq(lw));  // open: gt, lt
  assign bit_extender_1_out = {{24{DMEMOut[7]}}, DMEMOut[7:0]};  // Bit_Extender bit_extender_1
  and and_1 (and_1_out, rem0, lb);
  and and_2 (and_2_out, rem1, lb);
  assign bit_extender_2_out = {{24{DMEMOut[15]}}, DMEMOut[15:8]};  // Bit_Extender bit_extender_2
  Multiplexer #(.width(32), .enable("false")) multiplexer_5 (
    .in0(DMEMOut), .in1(bit_extender_1_out), .out(DMEMOutNew), .sel(and_1_out));
  Multiplexer #(.width(32), .enable("false")) multiplexer_6 (
    .in0(DMEMOut), .in1(bit_extender_2_out), .out(DMEMOutNew), .sel(and_2_out));
  // mem_main DMEM: pin names not known; wires that end beside it: ALUOut, ReadData2, MemRW, CLOCK, DMEMOut
  and and_3 (and_3_out, rem2, lb);
  assign bit_extender_3_out = {{24{DMEMOut[23]}}, DMEMOut[23:16]};  // Bit_Extender bit_extender_3
  assign bit_extender_4_out = {{24{DMEMOut[31]}}, DMEMOut[31:24]};  // Bit_Extender bit_extender_4
  and and_4 (and_4_out, rem3, lb);
  Multiplexer #(.width(32), .enable("false")) multiplexer_7 (
    .in0(DMEMOut), .in1(bit_extender_3_out), .out(DMEMOutNew), .sel(and_3_out));
  Multiplexer #(.width(32), .enable("false")) multiplexer_8 (
    .in0(DMEMOut), .in1(bit_extender_4_out), .out(DMEMOutNew), .sel(and_4_out));
  Adder #(.width(32)) adder_2 (.a(PCWithPipeline), .b(32'h4), .out(adder_2_out));  // open: cin, cout
  Multiplexer #(.select(2), .width(32), .enable("false")) multiplexer_9 (
    .in0(adder_2_out), .in1(ALUOut), .in2(DMEMOutNew), .out(wb), .sel(WBSel));  // open: in3
  assign bit_extender_5_out = {{16{DMEMOut[15]}}, DMEMOut[15:0]};  // Bit_Extender bit_extender_5
  and and_5 (and_5_out, rem0, lh);
  and and_6 (and_6_out, rem2, lh);
  assign bit_extender_6_out = {{16{DMEMOut[31]}}, DMEMOut[31:16]};  // Bit_Extender bit_extender_6
  Multiplexer #(.width(32), .enable("false")) multiplexer_10 (
    .in0(DMEMOut), .in1(bit_extender_5_out), .out(DMEMOutNew), .sel(and_5_out));
  Multiplexer #(.width(32), .enable("false")) multiplexer_11 (
    .in0(DMEMOut), .in1(bit_extender_6_out), .out(DMEMOutNew), .sel(and_6_out));

  // Other names for the same wires on the sheet: clk = CLOCK; PROGRAM_COUNTER[31:0] = FETCH_ADDRESS

  // Notes on the sheet:
  //   Output
  //   Inputs/Outputs from run.circ. DO NOT MOVE THESE.
  //   Inputs
  //   7 cases: lb 0, lb 1, lb 2, lb 3, lh 0, lh 2, lw 0
  //   Inputs/Outputs from run.circ. DO NOT MOVE THESE.
endmodule

module ImmGenerator (
  input  [31:0] Instruction,
  input  [4:0] ImmSel,
  output [31:0] out_3
);

  wire [31:0] ITypeOut, SBTypeOut, STypeOut, UJTypeOut;

  Multiplexer #(.select(5), .width(32), .enable("false")) multiplexer_1 (
    .in0(ITypeOut), .in4(ITypeOut), .in5({Instruction[31:12], {12{1'b0}}}), .in6(ITypeOut), .in8(STypeOut),
    .in13({Instruction[31:12], {12{1'b0}}}), .in24(SBTypeOut), .in25(ITypeOut), .in27(UJTypeOut),
    .in28(ITypeOut), .out(out_3), .sel(ImmSel));  // open: in1, in2, in3, in7, in9, in10, in11, in12, in14, in15, in16, in17, in18, in19, in20, in21, in22, in23, in26, in29, in30, in31
  assign ITypeOut = {{20{Instruction[31]}}, Instruction[31:20]};  // Bit_Extender bit_extender_1
  assign STypeOut = {{20{Instruction[31]}}, {Instruction[31:25], Instruction[11:7]}};  // Bit_Extender bit_extender_2
  assign SBTypeOut = {{19{Instruction[31]}}, {Instruction[31], Instruction[7], Instruction[30:25], Instruction[11:8], 1'b0}};  // Bit_Extender bit_extender_3
  assign UJTypeOut = {{11{Instruction[31]}}, {Instruction[31], Instruction[19:12], Instruction[20], Instruction[30:21], 1'b0}};  // Bit_Extender bit_extender_4

  // Other names for the same wires on the sheet: UTypeOut[31:12] = Instruction[31:12]

  // Notes on the sheet:
  //   opcode[6:2]
  //   I: 00000,00100,00110,11001,11100
  //   S:01000
  //   U:01101,00101,01101
  //   SB:11000
  //   UJ:11011
endmodule

module Control (
  input  [31:0] Instruction,
  input  [31:0] ReadData1,
  input  [31:0] ReadData2,
  output PCSel,
  output RegWEn,
  output BrEq,
  output BrLt,
  output ASel,
  output BSel,
  output [3:0] ALUSel,
  output MemRW,
  output [1:0] WBSel
);

  wire and1, and_1_out, and_2_out, and_3_out, and_4_out, and_5_out, and_6_out, and_7_out, and_8_out,
       and_9_out, and_10_out, and_12_out, and_13_out, and_16_out, and_17_out, and_19_out, and_20_out,
       and_21_out, and_22_out, BrUn, bsel13, comparator_1_eq, comparator_2_eq, comparator_3_eq,
       comparator_4_eq, comparator_5_eq, comparator_6_eq, comparator_13_eq, comparator_14_eq,
       comparator_15_eq, comparator_16_eq, comparator_17_eq, comparator_18_eq, comparator_19_eq,
       comparator_20_eq, comparator_21_eq, comparator_24_eq, comparator_25_eq, comparator_26_eq,
       comparator_27_eq, comparator_28_eq, comparator_29_eq, comparator_30_eq, comparator_31_eq,
       comparator_32_eq, comparator_33_eq, comparator_34_eq, comparator_35_eq, comparator_36_eq,
       comparator_37_eq, comparator_38_eq, comparator_39_eq, comparator_40_eq, comparator_41_eq,
       comparator_42_eq, comparator_43_eq, comparator_44_eq, comparator_45_eq, comparator_46_eq, divu8, I03,
       I13, I67, mul10, mulh14, mulhu11, not_1_out, or2, or_1_out, or_5_out, or_10_out, remu9, RType, SBType,
       sll6, slt7, sra5, srl4, sub12, UJType, vaddh15, xor3;
  wire [1:0] multiplexer_10_out;
  wire [3:0] multiplexer_1_out, multiplexer_2_out, multiplexer_3_out, multiplexer_4_out, multiplexer_5_out,
       multiplexer_6_out, multiplexer_7_out, multiplexer_8_out, multiplexer_9_out, multiplexer_12_out,
       multiplexer_13_out, multiplexer_14_out, multiplexer_15_out, multiplexer_16_out;

  Comparator #(.width(3)) comparator_1 (.a(Instruction[14:12]), .b(3'b000), .eq(comparator_1_eq));  // open: gt, lt
  Comparator #(.width(3)) comparator_2 (.a(Instruction[14:12]), .b(3'b100), .eq(comparator_2_eq));  // open: gt, lt
  Comparator #(.width(3)) comparator_3 (.a(Instruction[14:12]), .b(3'b110), .eq(comparator_3_eq));  // open: gt, lt
  Comparator #(.width(3)) comparator_4 (.a(Instruction[14:12]), .b(3'b001), .eq(comparator_4_eq));  // open: gt, lt
  and and_1 (and_1_out, SBType, comparator_1_eq, BrEq);
  and and_2 (and_2_out, SBType, comparator_3_eq, BrLt);
  not not_1 (not_1_out, BrEq);
  and and_3 (and_3_out, SBType, comparator_2_eq, BrLt);
  and and_4 (and_4_out, SBType, comparator_4_eq, not_1_out);
  or or_1 (or_1_out, and_1_out, and_3_out, and_2_out, and_4_out);
  or or_2 (PCSel, UJType, I67, or_1_out);
  Comparator #(.width(3)) comparator_5 (.a(Instruction[14:12]), .b(3'b110), .eq(comparator_5_eq));  // open: gt, lt
  Comparator #(.width(7)) comparator_6 (.a(Instruction[31:25]), .b(7'b0000001), .eq(comparator_6_eq));  // open: gt, lt
  or or_3 (ASel, UJType, SBType);
  and and_5 (and_5_out, SBType, comparator_5_eq);
  and and_6 (and_6_out, RType, comparator_6_eq);
  or or_4 (BrUn, and_5_out, and_6_out);
  BranchComparator branchcomparator_1 (.rs1(ReadData1), .rs2(ReadData2), .BrUn(BrUn), .BrEq(BrEq), .BrLt(BrLt));
  Comparator #(.width(7)) comparator_7 (.a(Instruction[6:0]), .b(7'b1101111), .eq(UJType));  // open: gt, lt
  Comparator #(.width(7)) comparator_8 (.a(Instruction[6:0]), .b(7'b1100111), .eq(I67));  // open: gt, lt
  Comparator #(.width(7)) comparator_9 (.a(Instruction[6:0]), .b(7'b0110011), .eq(RType));  // open: gt, lt
  Comparator #(.width(7)) comparator_10 (.a(Instruction[6:0]), .b(7'b0100011), .eq(MemRW));  // open: gt, lt
  Comparator #(.width(7)) comparator_11 (.a(Instruction[6:0]), .b(7'b1100011), .eq(SBType));  // open: gt, lt
  Comparator #(.width(7)) comparator_12 (.a(Instruction[6:0]), .b(7'b0110111), .eq(bsel13));  // open: gt, lt
  Comparator #(.width(3)) comparator_13 (.a(Instruction[14:12]), .b(3'b111), .eq(comparator_13_eq));  // open: gt, lt
  Comparator #(.width(7)) comparator_14 (.a(Instruction[31:25]), .b({7{1'b0}}), .eq(comparator_14_eq));  // open: gt, lt
  Comparator #(.width(3)) comparator_15 (.a(Instruction[14:12]), .b(3'b111), .eq(comparator_15_eq));  // open: gt, lt
  Comparator #(.width(3)) comparator_16 (.a(Instruction[14:12]), .b(3'b101), .eq(comparator_16_eq));  // open: gt, lt
  Comparator #(.width(7)) comparator_17 (.a(Instruction[31:25]), .b({7{1'b0}}), .eq(comparator_17_eq));  // open: gt, lt
  Comparator #(.width(3)) comparator_18 (.a(Instruction[14:12]), .b(3'b101), .eq(comparator_18_eq));  // open: gt, lt
  Comparator #(.width(7)) comparator_19 (.a(Instruction[31:25]), .b({7{1'b0}}), .eq(comparator_19_eq));  // open: gt, lt
  Comparator #(.width(3)) comparator_20 (.a(Instruction[14:12]), .b(3'b000), .eq(comparator_20_eq));  // open: gt, lt
  Comparator #(.width(7)) comparator_21 (
    .a(Instruction[31:25]), .b(7'b0000001), .eq(comparator_21_eq));  // open: gt, lt
  not not_2 (RegWEn, or_5_out);
  or or_5 (or_5_out, MemRW, SBType);
  and and_7 (and_7_out, RType, comparator_13_eq, comparator_14_eq);
  and and_8 (and_8_out, I13, comparator_15_eq);
  and and_9 (and_9_out, RType, comparator_16_eq, comparator_17_eq);
  and and_10 (and_10_out, I13, comparator_18_eq, comparator_19_eq);
  and and_11 (mul10, RType, comparator_20_eq, comparator_21_eq);
  Comparator #(.width(7)) comparator_22 (.a(Instruction[6:0]), .b(7'b0000011), .eq(I03));  // open: gt, lt
  Comparator #(.width(7)) comparator_23 (.a(Instruction[6:0]), .b(7'b0010011), .eq(I13));  // open: gt, lt
  not not_3 (BSel, RType);
  or or_6 (and1, and_7_out, and_8_out);
  or or_7 (srl4, and_9_out, and_10_out);
  Multiplexer #(.width(4), .enable("false")) multiplexer_1 (
    .in0(4'b0000), .in1(4'b0001), .out(multiplexer_1_out), .sel(and1));
  Multiplexer #(.width(4), .enable("false")) multiplexer_2 (
    .in0(multiplexer_1_out), .in1(4'b0010), .out(multiplexer_2_out), .sel(or2));
  Comparator #(.width(3)) comparator_24 (.a(Instruction[14:12]), .b(3'b110), .eq(comparator_24_eq));  // open: gt, lt
  Comparator #(.width(3)) comparator_25 (.a(Instruction[14:12]), .b(3'b110), .eq(comparator_25_eq));  // open: gt, lt
  Comparator #(.width(3)) comparator_26 (.a(Instruction[14:12]), .b(3'b101), .eq(comparator_26_eq));  // open: gt, lt
  Comparator #(.width(7)) comparator_27 (
    .a(Instruction[31:25]), .b(7'b0100000), .eq(comparator_27_eq));  // open: gt, lt
  Comparator #(.width(3)) comparator_28 (.a(Instruction[14:12]), .b(3'b011), .eq(comparator_28_eq));  // open: gt, lt
  Multiplexer #(.width(4), .enable("false")) multiplexer_3 (
    .in0(multiplexer_2_out), .in1(4'b0011), .out(multiplexer_3_out), .sel(xor3));
  and and_12 (and_12_out, RType, comparator_24_eq);
  and and_13 (and_13_out, I13, comparator_25_eq);
  and and_14 (sra5, I13, comparator_26_eq, comparator_27_eq);
  and and_15 (mulhu11, RType, comparator_28_eq);
  Multiplexer #(.width(4), .enable("false")) multiplexer_4 (
    .in0(multiplexer_3_out), .in1(4'b0100), .out(multiplexer_4_out), .sel(srl4));
  or or_8 (or2, and_12_out, and_13_out);
  Multiplexer #(.width(4), .enable("false")) multiplexer_5 (
    .in0(multiplexer_4_out), .in1(4'b0101), .out(multiplexer_5_out), .sel(sra5));
  Multiplexer #(.width(4), .enable("false")) multiplexer_6 (
    .in0(multiplexer_5_out), .in1(4'b0110), .out(multiplexer_6_out), .sel(sll6));
  Multiplexer #(.width(4), .enable("false")) multiplexer_7 (
    .in0(multiplexer_6_out), .in1(4'b0111), .out(multiplexer_7_out), .sel(slt7));
  Comparator #(.width(3)) comparator_29 (.a(Instruction[14:12]), .b(3'b001), .eq(comparator_29_eq));  // open: gt, lt
  Comparator #(.width(7)) comparator_30 (.a(Instruction[31:25]), .b({7{1'b0}}), .eq(comparator_30_eq));  // open: gt, lt
  Comparator #(.width(3)) comparator_31 (.a(Instruction[14:12]), .b(3'b001), .eq(comparator_31_eq));  // open: gt, lt
  Comparator #(.width(7)) comparator_32 (.a(Instruction[31:25]), .b({7{1'b0}}), .eq(comparator_32_eq));  // open: gt, lt
  Comparator #(.width(3)) comparator_33 (.a(Instruction[14:12]), .b(3'b000), .eq(comparator_33_eq));  // open: gt, lt
  Comparator #(.width(7)) comparator_34 (
    .a(Instruction[31:25]), .b(7'b0100000), .eq(comparator_34_eq));  // open: gt, lt
  Multiplexer #(.width(4), .enable("false")) multiplexer_8 (
    .in0(multiplexer_7_out), .in1(4'b1000), .out(multiplexer_8_out), .sel(divu8));
  Comparator #(.width(3)) comparator_35 (.a(Instruction[14:12]), .b(3'b100), .eq(comparator_35_eq));  // open: gt, lt
  Comparator #(.width(3)) comparator_36 (.a(Instruction[14:12]), .b(3'b100), .eq(comparator_36_eq));  // open: gt, lt
  and and_16 (and_16_out, RType, comparator_29_eq, comparator_30_eq);
  or or_9 (sll6, and_16_out, and_17_out);
  and and_17 (and_17_out, I13, comparator_31_eq, comparator_32_eq);
  and and_18 (sub12, RType, comparator_33_eq, comparator_34_eq);
  or or_10 (or_10_out, UJType, I67);
  Multiplexer #(.width(4), .enable("false")) multiplexer_9 (
    .in0(multiplexer_8_out), .in1(4'b1001), .out(multiplexer_9_out), .sel(remu9));
  and and_19 (and_19_out, RType, comparator_35_eq);
  or or_11 (xor3, and_19_out, and_20_out);
  and and_20 (and_20_out, I13, comparator_36_eq);
  Multiplexer #(.width(2), .enable("false")) multiplexer_10 (
    .in0(2'b01), .in1(2'b00), .out(multiplexer_10_out), .sel(or_10_out));
  Multiplexer #(.width(2), .enable("false")) multiplexer_11 (
    .in0(multiplexer_10_out), .in1(2'b10), .out(WBSel), .sel(I03));
  Multiplexer #(.width(4), .enable("false")) multiplexer_12 (
    .in0(multiplexer_9_out), .in1(4'b1010), .out(multiplexer_12_out), .sel(mul10));
  Multiplexer #(.width(4), .enable("false")) multiplexer_13 (
    .in0(multiplexer_12_out), .in1(4'b1011), .out(multiplexer_13_out), .sel(mulhu11));
  Comparator #(.width(3)) comparator_37 (.a(Instruction[14:12]), .b(3'b010), .eq(comparator_37_eq));  // open: gt, lt
  Comparator #(.width(3)) comparator_38 (.a(Instruction[14:12]), .b(3'b010), .eq(comparator_38_eq));  // open: gt, lt
  Multiplexer #(.width(4), .enable("false")) multiplexer_14 (
    .in0(multiplexer_13_out), .in1(4'b1100), .out(multiplexer_14_out), .sel(sub12));
  and and_21 (and_21_out, RType, comparator_37_eq);
  and and_22 (and_22_out, I13, comparator_38_eq);
  Comparator #(.width(3)) comparator_39 (.a(Instruction[14:12]), .b(3'b000), .eq(comparator_39_eq));  // open: gt, lt
  Comparator #(.width(7)) comparator_40 (
    .a(Instruction[31:25]), .b(7'b0001111), .eq(comparator_40_eq));  // open: gt, lt
  Multiplexer #(.width(4), .enable("false")) multiplexer_15 (
    .in0(multiplexer_14_out), .in1(4'b1101), .out(multiplexer_15_out), .sel(bsel13));
  or or_12 (slt7, and_21_out, and_22_out);
  and and_23 (vaddh15, RType, comparator_39_eq, comparator_40_eq);
  Multiplexer #(.width(4), .enable("false")) multiplexer_16 (
    .in0(multiplexer_15_out), .in1(4'b1110), .out(multiplexer_16_out), .sel(mulh14));
  Multiplexer #(.width(4), .enable("false")) multiplexer_17 (
    .in0(multiplexer_16_out), .in1(4'b1111), .out(ALUSel), .sel(vaddh15));
  Comparator #(.width(3)) comparator_41 (.a(Instruction[14:12]), .b(3'b101), .eq(comparator_41_eq));  // open: gt, lt
  Comparator #(.width(7)) comparator_42 (
    .a(Instruction[31:25]), .b(7'b0000001), .eq(comparator_42_eq));  // open: gt, lt
  Comparator #(.width(3)) comparator_43 (.a(Instruction[14:12]), .b(3'b001), .eq(comparator_43_eq));  // open: gt, lt
  Comparator #(.width(7)) comparator_44 (
    .a(Instruction[31:25]), .b(7'b0000001), .eq(comparator_44_eq));  // open: gt, lt
  and and_24 (divu8, RType, comparator_41_eq, comparator_42_eq);
  Comparator #(.width(3)) comparator_45 (.a(Instruction[14:12]), .b(3'b111), .eq(comparator_45_eq));  // open: gt, lt
  Comparator #(.width(7)) comparator_46 (
    .a(Instruction[31:25]), .b(7'b0000001), .eq(comparator_46_eq));  // open: gt, lt
  and and_25 (mulh14, RType, comparator_43_eq, comparator_44_eq);
  and and_26 (remu9, RType, comparator_45_eq, comparator_46_eq);

  // Other names for the same wires on the sheet: UType = bsel13; Input1[31:0] = Instruction;
  //   Opcode[6:0] = Instruction[6:0]; rd[4:0] = Instruction[11:7]; funct3[2:0] = Instruction[14:12];
  //   rs1[4:0] = Instruction[19:15]; rs2[4:0] = Instruction[24:20]; funct7[6:0] = Instruction[31:25]; SType = MemRW

  // Notes on the sheet:
  //   Input and Opcode
  //   Outputs
  //   WBSel: three muxes
  //   Add support for vaddh in ALU
  //   Bug: slti, branch comparator should be comparing rs1 and an imm
  //   ALUSel: 15 muxes
  //   2: mem
  //   0: PC+4, jal(r)
  //   Otherwise: ALUOut
endmodule

module BranchComparator (
  input  [31:0] rs1,
  input  [31:0] rs2,
  input  BrUn,
  output BrEq,
  output BrLt
);

  wire comparator_2_lt, comparator_3_lt;

  Comparator #(.width(32)) comparator_1 (.a(rs1), .b(rs2), .eq(BrEq));  // open: gt, lt
  Comparator #(.width(32)) comparator_2 (.a(rs1), .b(rs2), .lt(comparator_2_lt));  // open: gt, eq
  Comparator #(.width(32), .mode("unsigned")) comparator_3 (.a(rs1), .b(rs2), .lt(comparator_3_lt));  // open: gt, eq
  Multiplexer #(.enable("false")) multiplexer_1 (.in0(comparator_2_lt), .in1(comparator_3_lt), .out(BrLt), .sel(BrUn));
endmodule
